# Fritzing sketch open-race-scale-pi-hat-v1 (saved by Fritzing 0.9.3b)
circuit board: 8.53488cm x 5.63626cm

parts:
  FL = screw terminal, 4 pins
  FR = screw terminal, 4 pins
  RL = screw terminal, 4 pins
  RR = screw terminal, 4 pins
  3v = Pad [width=2 height=2 connect=center]
  P1 = Pad [width=2 height=2 connect=center]
  5v = Pad [width=2 height=2 connect=center]
  Ext = Pad [width=2 height=2 connect=center]
  P1_2 = Pad [width=2 height=2 connect=center]
  P0 = male pin header, 2 pins [form="♂ (male)"]
  J1 = male pin header, 3 pins [form="♂ (male)"]
  J2 = male pin header, 3 pins [form="♂ (male)"]
  Raspberry_Pi_1 = Raspberry Pi 3 [part_number=RPI-3-V1.2]
  J3 = male pin header, 3 pins [form="♂ (male)"]
  J4 = male pin header, 3 pins [form="♂ (male)"]
  J5 = male pin header, 3 pins [form="♂ (male)"]
  J6 = male pin header, 3 pins [form="♂ (male)"]
  J7 = male pin header, 3 pins [form="♂ (male)"]
  J8 = male pin header, 3 pins [form="♂ (male)"]
  LC1 = HX711 Weighing Sensor Module [part_number=XFW-HX711]
  LC2 = HX711 Weighing Sensor Module [part_number=XFW-HX711]
  LC3 = HX711 Weighing Sensor Module [part_number=XFW-HX711]
  LC4 = HX711 Weighing Sensor Module [part_number=XFW-HX711]

nets:
  N1: FL.pin1, J2.pin2
  N2: FL.pin2, J1.pin2
  N3: FL.pin3, LC1.E-
  N4: FL.pin4, LC1.E+
  N5: FR.pin1, J4.pin2
  N6: FR.pin2, J3.pin2
  N7: FR.pin3, LC2.E-
  N8: FR.pin4, LC2.E+
  N9: RL.pin1, J6.pin2
  N10: RL.pin2, J5.pin2
  N11: RL.pin3, LC3.E-
  N12: RL.pin4, LC3.E+
  N13: RR.pin1, J8.pin2
  N14: RR.pin2, J7.pin2
  N15: RR.pin3, LC4.E-
  N16: RR.pin4, LC4.E+
  N17: 3v.pad, Raspberry_Pi_1.3v3
  VCC: P1.pad, 5v.pad, P1_2.pad, Raspberry_Pi_1.5V, LC1.VCC, LC2.VCC, LC3.VCC, LC4.VCC
  5V: Ext.pad, P0.pin2
  GND: P0.pin1, Raspberry_Pi_1.GND, LC1.GND, LC2.GND, LC3.GND, LC4.GND
  N18: J1.pin1, LC1.A-
  N19: J1.pin3, LC1.B-
  N20: J2.pin1, LC1.A+
  N21: J2.pin3, LC1.B+
  N22: Raspberry_Pi_1.GPIO17, LC1.DO/RX
  N23: Raspberry_Pi_1.GPIO27, LC1.CK/TX
  N24: Raspberry_Pi_1.GPIO22, LC2.DO/RX
  N25: Raspberry_Pi_1.GPIO5, LC3.DO/RX
  N26: Raspberry_Pi_1.GPIO6, LC3.CK/TX
  N27: Raspberry_Pi_1.GPIO26, LC4.CK/TX
  N28: Raspberry_Pi_1.GPIO16, LC4.DO/RX
  N29: Raspberry_Pi_1.GPIO23, LC2.CK/TX
  N30: J3.pin1, LC2.A-
  N31: J3.pin3, LC2.B-
  N32: J4.pin1, LC2.A+
  N33: J4.pin3, LC2.B+
  N34: J5.pin1, LC3.A-
  N35: J5.pin3, LC3.B-
  N36: J6.pin1, LC3.A+
  N37: J6.pin3, LC3.B+
  N38: J7.pin1, LC4.A-
  N39: J7.pin3, LC4.B-
  N40: J8.pin1, LC4.A+
  N41: J8.pin3, LC4.B+

notes:
  Red -> E+
  Black -> E-
  Green -> A+
  White -> A-
  To FR Load Cell
  To RL Load Cell
  To RR Load Cell
  E+
  Ext Power
  (optional)
  Open Race Scale V1.0 Rev 02
  Gnd
  To FL Load Cell
  Jumper Pins to
  Select Channel
  E-
  S-
  S+

custom parts:
  HX711 Weighing Sensor Module: HX711 is a precision 24-bit analog-to-digital converter (ADC) designed for weigh scales and industrial control applications to interface directly with a bridge sensor.
