# Fritzing sketch open-race-scale-schem-v1-pcb-only (saved by Fritzing 0.9.3b)
circuit board: 8.53488cm x 5.63626cm

parts:
  Part1 = HX711 Weighing Sensor Module
  Part2 = HX711 Weighing Sensor Module
  Part3 = HX711 Weighing Sensor Module
  Part4 = HX711 Weighing Sensor Module
  J1 = double row female pin header, 40 pins [form="♀ (female)"]
  LC1 = screw terminal, 4 pins
  LC2 = screw terminal, 4 pins
  LC3 = screw terminal, 4 pins
  LC4 = screw terminal, 4 pins

nets:
  VCC: Part1.VCC, Part2.VCC, Part3.VCC, Part4.VCC, J1.pin40
  GND: Part1.GND, Part2.GND, Part3.GND, Part4.GND, J1.pin20
  N1: Part1.DO/RX, J1.pin6
  N2: Part1.CK/TX, J1.pin7
  N3: Part1.E+, LC1.pin4
  N4: Part1.E-, LC1.pin3
  N5: Part1.A+, LC1.pin2
  N6: Part1.A-, LC1.pin1
  N7: Part2.DO/RX, J1.pin8
  N8: Part2.CK/TX, J1.pin33
  N9: Part2.E+, LC2.pin4
  N10: Part2.E-, LC2.pin3
  N11: Part2.A+, LC2.pin2
  N12: Part2.A-, LC2.pin1
  N13: Part3.DO/RX, J1.pin15
  N14: Part3.CK/TX, J1.pin16
  N15: Part3.E+, LC3.pin4
  N16: Part3.E-, LC3.pin3
  N17: Part3.A+, LC3.pin2
  N18: Part3.A-, LC3.pin1
  N19: Part4.DO/RX, J1.pin23
  N20: Part4.CK/TX, J1.pin19
  N21: Part4.E+, LC4.pin4
  N22: Part4.E-, LC4.pin3
  N23: Part4.A+, LC4.pin2
  N24: Part4.A-, LC4.pin1

notes:
  Red -> E+
  Black -> E-
  Green -> A+
  White -> A-
