# Fritzing sketch open-race-scale-schem-v1 (saved by Fritzing 0.9.3b)

parts:
  Part1 = HX711 Weighing Sensor Module
  Part2 = HX711 Weighing Sensor Module
  Part3 = HX711 Weighing Sensor Module
  Part4 = HX711 Weighing Sensor Module
  Load_Cell1 = Load Cell - Red/white/black/green
  Load_Cell2 = Load Cell - Red/white/black/green
  Load_Cell3 = Load Cell - Red/white/black/green
  Load_Cell4 = Load Cell - Red/white/black/green
  Raspberry_Pi_1 = Raspberry Pi 3 [part_number=RPI-3-V1.2]

nets:
  VCC: Part1.VCC, Part2.VCC, Part3.VCC, Part4.VCC, Raspberry_Pi_1.5V
  GND: Part1.GND, Part2.GND, Part3.GND, Part4.GND, Raspberry_Pi_1.GND
  N1: Part1.DO/RX, Raspberry_Pi_1.GPIO5
  N2: Part1.CK/TX, Raspberry_Pi_1.GPIO6
  N3: Part1.E+, Load_Cell1.wire1
  N4: Part1.E-, Load_Cell1.wire3
  N5: Part1.A+, Load_Cell1.wire4
  N6: Part1.A-, Load_Cell1.wire2
  N7: Part2.DO/RX, Raspberry_Pi_1.GPIO16
  N8: Part2.CK/TX, Raspberry_Pi_1.GPIO17
  N9: Part2.E+, Load_Cell2.wire1
  N10: Part2.E-, Load_Cell2.wire3
  N11: Part2.A+, Load_Cell2.wire4
  N12: Part2.A-, Load_Cell2.wire2
  N13: Part3.DO/RX, Raspberry_Pi_1.GPIO22
  N14: Part3.CK/TX, Raspberry_Pi_1.GPIO23
  N15: Part3.E+, Load_Cell3.wire1
  N16: Part3.E-, Load_Cell3.wire3
  N17: Part3.A+, Load_Cell3.wire4
  N18: Part3.A-, Load_Cell3.wire2
  N19: Part4.DO/RX, Raspberry_Pi_1.GPIO24
  N20: Part4.CK/TX, Raspberry_Pi_1.GPIO25
  N21: Part4.E+, Load_Cell4.wire1
  N22: Part4.E-, Load_Cell4.wire3
  N23: Part4.A+, Load_Cell4.wire4
  N24: Part4.A-, Load_Cell4.wire2

notes:
  Red -> E+
  Black -> E-
  Green -> A+
  White -> A-

custom parts:
  Load Cell - Red/white/black/green: A rectangle load cell/weighting pressure Sensor with four wires - Red, white, black, green. Normally corresponding with E+, E-, A+, A- respectively.
